// Logisim project Exp2_1.circ as structural Verilog: 1 circuit, main circuit main
module main (
  input  in_1,
  input  in_2,
  output Sum,
  output out_4
);

  wire and_1_out, xor_1_out;

  xor xor_1 (xor_1_out, in_1, in_2);
  and and_1 (and_1_out, in_1, in_2);

  // Notes on the sheet:
  //   XOR
  //   25BIT123
  //   Half adder Circuit
  //   AND
endmodule
