// Logisim project Exp2_2.circ as structural Verilog: 1 circuit, main circuit main
module main (
  input  in_1,
  input  in_2,
  input  in_3,
  output Sum,
  output out_5
);

  wire and_1_out, and_2_out, or_1_out, xor_1_out, xor_2_out;

  xor xor_1 (xor_1_out, in_1, in_2);
  and and_1 (and_1_out, in_3, xor_1_out);
  and and_2 (and_2_out, in_1, in_2);
  xor xor_2 (xor_2_out, xor_1_out, in_3);
  or or_1 (or_1_out, and_1_out, and_2_out);

  // Notes on the sheet:
  //   25BIT123
  //   Full adder Circuit
endmodule
