// Logisim project Exp2_3.circ as structural Verilog: 1 circuit, main circuit main
module main (
  input  A,
  input  B
);

  wire and_1_out, and_2_out, and_3_out, not_1_out, not_2_out, or_1_out;

  not not_1 (not_1_out, B);
  not not_2 (not_2_out, A);
  and and_1 (and_1_out, A, not_1_out);
  and and_2 (and_2_out, not_2_out, B);
  or or_1 (or_1_out, and_1_out, and_2_out);
  and and_3 (and_3_out, A, B);
  LED led_1 (.in(or_1_out));
  LED led_2 (.in(and_3_out));

  // Notes on the sheet:
  //   25BIT123
  //   Half adder circuit using basic gates
  //   Y=AB'+A'B
  //   Sum
  //   Carry out
endmodule
