// Logisim project NOR as AND.circ as structural Verilog: 1 circuit, main circuit main
module main (
  input  A,
  input  B
);

  wire nor_1_out, nor_2_out, nor_3_out;

  nor nor_1 (nor_1_out, A, A);
  nor nor_2 (nor_2_out, B, B);
  nor nor_3 (nor_3_out, nor_1_out, nor_2_out);

  // Notes on the sheet:
  //   A'
  //   B'
  //   NOR gates as AND gate
  //   25BIT123
  //   (A'+B')'=AB
endmodule
