// Logisim project full_adder_using_NAND_gates.circ as structural Verilog: 1 circuit, main circuit main
module main (
  input  A,
  input  B,
  input  C_in
);

  wire nand_1_out, nand_2_out, nand_3_out, nand_4_out, nand_5_out, nand_6_out, nand_7_out, nand_8_out,
       nand_9_out;

  nand nand_1 (nand_1_out, A, B);
  nand nand_2 (nand_2_out, A, nand_1_out);
  nand nand_3 (nand_3_out, nand_1_out, B);
  nand nand_4 (nand_4_out, nand_2_out, nand_3_out);
  nand nand_5 (nand_5_out, nand_4_out, C_in);
  nand nand_6 (nand_6_out, nand_4_out, nand_5_out);
  nand nand_7 (nand_7_out, nand_5_out, C_in);
  nand nand_8 (nand_8_out, nand_5_out, nand_1_out);
  LED led_1 (.in(nand_8_out));
  nand nand_9 (nand_9_out, nand_6_out, nand_7_out);
  LED led_2 (.in(nand_9_out));

  // Notes on the sheet:
  //   FULL ADDER USING NAND GATES
  //   25BIT123
  //   C_out
  //   SUM
endmodule
