// Logisim project full_adder_using_NOR_gates.circ as structural Verilog: 1 circuit, main circuit main
module main (
  input  in_1,
  input  in_2,
  input  in_3
);

  wire nor_1_out, nor_2_out, nor_3_out, nor_4_out, nor_5_out, nor_6_out, nor_7_out, nor_8_out, nor_9_out;

  nor nor_1 (nor_1_out, in_1, in_2);
  nor nor_2 (nor_2_out, in_1, nor_1_out);
  nor nor_3 (nor_3_out, nor_1_out, in_2);
  nor nor_4 (nor_4_out, nor_2_out, nor_3_out);
  nor nor_5 (nor_5_out, nor_4_out, in_3);
  nor nor_6 (nor_6_out, nor_4_out, nor_5_out);
  nor nor_7 (nor_7_out, nor_5_out, in_3);
  nor nor_8 (nor_8_out, nor_1_out, nor_5_out);
  LED led_1 (.in(nor_8_out));
  nor nor_9 (nor_9_out, nor_6_out, nor_7_out);
  LED led_2 (.in(nor_9_out));

  // Notes on the sheet:
  //   25BIT123
  //   FULL ADDER USING NOR GATES
endmodule
