// Logisim project full_adder_using_basic_gates.circ as structural Verilog: 1 circuit, main circuit main
module main (
  input  A,
  input  B,
  input  C_IN
);

  wire and_1_out, and_2_out, and_3_out, and_4_out, and_5_out, and_6_out, and_7_out, not_1_out, not_2_out,
       not_3_out, or_1_out, or_2_out;

  not not_1 (not_1_out, A);
  not not_2 (not_2_out, B);
  not not_3 (not_3_out, C_IN);
  and and_1 (and_1_out, A, B);
  and and_2 (and_2_out, B, C_IN);
  and and_3 (and_3_out, A, C_IN);
  and and_4 (and_4_out, not_1_out, not_2_out, C_IN);
  and and_5 (and_5_out, not_1_out, B, not_3_out);
  and and_6 (and_6_out, A, not_2_out, not_3_out);
  and and_7 (and_7_out, A, B, C_IN);
  or or_1 (or_1_out, and_1_out, and_2_out, and_3_out);
  LED led_1 (.in(or_1_out));
  or or_2 (or_2_out, and_4_out, and_5_out, and_6_out, and_7_out);
  LED led_2 (.in(or_2_out));

  // Notes on the sheet:
  //   25BIT123
  //   Full Adder using basic gates
  //   AB
  //   BC
  //   AC
  //   A'BC'
  //   AB'C'
  //   ABC
  //   A'B'C
  //   C_OUT
  //   SUM
endmodule
