// Logisim project half_adder_using_nand_gates.circ as structural Verilog: 1 circuit, main circuit main
module main (
  input  A,
  input  B
);

  wire nand_1_out, nand_2_out, nand_3_out, nand_4_out, nand_5_out;

  nand nand_1 (nand_1_out, A, B);
  nand nand_2 (nand_2_out, A, nand_1_out);
  nand nand_3 (nand_3_out, nand_1_out, B);
  nand nand_4 (nand_4_out, nand_1_out, nand_1_out);
  LED led_1 (.in(nand_4_out));
  nand nand_5 (nand_5_out, nand_2_out, nand_3_out);
  LED led_2 (.in(nand_5_out));

  // Notes on the sheet:
  //   25BIT123
  //   HALF ADDER USING NAND GATES
  //   A.B
  //   C_OUT
  //   A XOR B
  //   SUM
endmodule
